// Logisim project Bugputer.circ as structural Verilog: 3 circuits, main circuit main
module main (
  input  in_1,
  input  in_2
);

  wire toggle_11_tick_1_out_3, toggle_11_tick_2_out_3, toggle_11_tick_3_out_3, toggle_11_tick_4_out_3,
       toggle_11_tick_5_out_3;

  Toggle__11_Tick toggle_11_tick_1 (.in_1(in_1), .in_2(in_2), .out_3(toggle_11_tick_1_out_3));
  Toggle__11_Tick toggle_11_tick_2 (.in_1(toggle_11_tick_1_out_3), .in_2(in_2), .out_3(toggle_11_tick_2_out_3));
  Toggle__11_Tick toggle_11_tick_3 (.in_1(toggle_11_tick_2_out_3), .in_2(in_2), .out_3(toggle_11_tick_3_out_3));
  Toggle__11_Tick toggle_11_tick_4 (.in_1(toggle_11_tick_3_out_3), .in_2(in_2), .out_3(toggle_11_tick_4_out_3));
  Toggle__11_Tick toggle_11_tick_5 (.in_1(toggle_11_tick_4_out_3), .in_2(in_2), .out_3(toggle_11_tick_5_out_3));
endmodule

module Switch__4_Tick (
  input  Input,
  input  Reset,
  output Output
);

  wire not_1_out, or_1_out, or_2_out, or_3_out, or_4_out;

  buf or_1 (or_1_out, Reset);  // OR_Gate
  buf or_2 (or_2_out, Input);  // OR_Gate
  not not_1 (not_1_out, or_3_out);
  or or_3 (or_3_out, or_1_out, Reset);
  or or_4 (or_4_out, Input, or_2_out, Output);
  and and_1 (Output, or_4_out, not_1_out);
endmodule

module Toggle__11_Tick (
  input  in_1,
  input  in_2,
  output out_3
);

  wire and_1_out, and_2_out, and_3_out, not_1_out, not_2_out, or_1_out;

  not not_1 (not_1_out, in_1);
  not not_2 (not_2_out, in_1);
  Switch__4_Tick switch_4_tick_1 (.Input(and_1_out), .Reset(or_1_out), .Output(out_3));
  and and_1 (and_1_out, in_1, not_1_out);
  or or_1 (or_1_out, and_3_out, in_2);
  and and_2 (and_2_out, not_2_out, out_3);
  and and_3 (and_3_out, and_2_out, in_1);
endmodule
