// Logisim project meecrosoft.circ as structural Verilog
module bit__5_ticks (
  input  in,
  input  reset,
  output out
);

  wire not_2_out, or_1_out, or_2_out;

  or or_1 (or_1_out, reset, not_2_out);
  not not_1 (out, or_1_out);
  or or_2 (or_2_out, out, in);
  not not_2 (not_2_out, or_2_out);
endmodule

module byte__8_ticks (
  input  [7:0] in_1,
  input  in_2,
  output [7:0] out_3
);

  bit__5_ticks bit_5_ticks_1 (.in(in_1[0]), .reset(in_2), .out(out_3[0]));
  bit__5_ticks bit_5_ticks_2 (.in(in_1[1]), .reset(in_2), .out(out_3[1]));
  bit__5_ticks bit_5_ticks_3 (.in(in_1[2]), .reset(in_2), .out(out_3[2]));
  bit__5_ticks bit_5_ticks_4 (.in(in_1[3]), .reset(in_2), .out(out_3[3]));
  bit__5_ticks bit_5_ticks_5 (.in(in_1[4]), .reset(in_2), .out(out_3[4]));
  bit__5_ticks bit_5_ticks_6 (.in(in_1[5]), .reset(in_2), .out(out_3[5]));
  bit__5_ticks bit_5_ticks_7 (.in(in_1[6]), .reset(in_2), .out(out_3[6]));
  bit__5_ticks bit_5_ticks_8 (.in(in_1[7]), .reset(in_2), .out(out_3[7]));
endmodule
