// Logisim project templeOS2.circ as structural Verilog
module bit_memory (
  input  in_1,
  input  in_2,
  input  in_3,
  input  in_4,
  output out_5
);

  wire and_1_out, not_1_out, not_2_out, or_1_out, or_2_out;

  and and_1 (and_1_out, in_4, in_2);
  not not_1 (not_1_out, or_2_out);
  not not_2 (not_2_out, or_1_out);
  or or_1 (or_1_out, and_1_out, not_1_out);
  or or_2 (or_2_out, in_3, not_2_out);
  and and_2 (out_5, in_1, or_1_out);
endmodule

module _8_bit_memory (
  input  read,
  input  [7:0] in_2,
  input  store,
  input  reset,
  output [7:0] out_5
);

  bit_memory bit_memory_1 (.in_2(in_2[0]), .in_3(reset), .out_5(out_5[0]), .in_1(read), .in_4(store));
  bit_memory bit_memory_2 (.in_2(in_2[1]), .in_3(reset), .out_5(out_5[1]), .in_1(read), .in_4(store));
  bit_memory bit_memory_3 (.in_2(in_2[2]), .in_3(reset), .out_5(out_5[2]), .in_1(read), .in_4(store));
  bit_memory bit_memory_4 (.in_2(in_2[3]), .in_3(reset), .out_5(out_5[3]), .in_1(read), .in_4(store));
  bit_memory bit_memory_5 (.in_2(in_2[4]), .in_3(reset), .out_5(out_5[4]), .in_1(read), .in_4(store));
  bit_memory bit_memory_6 (.in_2(in_2[5]), .in_3(reset), .out_5(out_5[5]), .in_1(read), .in_4(store));
  bit_memory bit_memory_7 (.in_2(in_2[6]), .in_3(reset), .out_5(out_5[6]), .in_1(read), .in_4(store));
  bit_memory bit_memory_8 (.in_2(in_2[7]), .in_3(reset), .out_5(out_5[7]), .in_1(read), .in_4(store));
endmodule
