// Logisim project testing.circ as structural Verilog: 14 circuits, main circuit main
module main (
  input  in_1,
  input  in_2,
  input  in_3,
  input  [15:0] in_4,
  input  [15:0] in_5,
  output [15:0] out_6,
  output out_7
);

  wire button_3_out, button_4_out, button_out, C_out, counter_1_out_4, counter_2_out_4,
       n4_bit_to_bool_1_out_2, n8_counter_1_out_3, n8_counter_1_out_4, n8_counter_1_out_5,
       n8_counter_1_out_6, n8_counter_1_out_7, n8_counter_1_out_8, n8_counter_1_out_9, n8_counter_1_out_10,
       not_1_out, x_out;
  wire [2:0] base10_to_display_5_out_2_2, base10_to_display_6_out_2_2, base10_to_display_7_out_2_2,
       counter_1_out_3;
  wire [3:0] _4_bit_out_2, base10_to_display_5_out_2, base10_to_display_6_out_2, base10_to_display_7_out_2,
       n4_bit_gateway_1_out_3, n4_bit_gateway_2_out_3, n4_bit_gateway_3_out_3, n4_bit_gateway_4_out_3,
       n4_bit_gateway_5_out_3, n4_bit_gateway_6_out_3, n4_bit_gateway_7_out_3, n4_bit_gateway_8_out_3,
       n4_bit_storage_1_out_3, n4_bit_storage_2_out_3, n4_bit_storage_3_out_3, n4_bit_storage_4_out_3,
       n4_bit_storage_5_out_3, n4_bit_storage_6_out_3, n4_bit_storage_7_out_3, n4_bit_storage_8_out_3;
  wire [6:0] base10_to_display_1_out_2, base10_to_display_2_out_2, base10_to_display_3_out_2,
       base10_to_display_4_out_2, base10_to_display_8_out_2, base10_to_display_9_out_2;
  wire [9:0] _0_out, n4_bit_to_base10_1_out_2, n4_bit_to_base10_2_out_2, n4_bit_to_base10_3_out_2,
       n4_bit_to_base10_4_out_2, n4_bit_to_base10_5_out_2, n4_bit_to_base10_6_out_2,
       n4_bit_to_base10_7_out_2, n4_bit_to_base10_8_out_2, n4_bit_to_base10_9_out_2;

  Button _1 (.out(_0_out[1]));
  Button _4 (.out(_0_out[4]));
  Button _7 (.out(_0_out[7]));
  Button _0 (.out(_0_out[0]));
  Button button (.out(button_out));
  Button x (.out(x_out));
  Button _2 (.out(_0_out[2]));
  Button _3 (.out(_0_out[3]));
  Button _5 (.out(_0_out[5]));
  Button _6 (.out(_0_out[6]));
  Button _8 (.out(_0_out[8]));
  Button _9 (.out(_0_out[9]));
  Button C (.out(C_out));
  Button button_2 ();  // open: out
  Button button_3 (.out(button_3_out));
  Button button_4 (.out(button_4_out));
  base10_to_4_bit _4_bit (.in_1(_0_out), .out_2(_4_bit_out_2));
  bit_storage bit_storage_1 (.store(button_out), .reset(C_out));  // open: out_3
  bit_storage bit_storage_2 (.store(button_3_out), .reset(C_out));  // open: out_3
  bit_storage bit_storage_3 (.store(x_out), .reset(C_out));  // open: out_3
  bit_storage bit_storage_4 (.store(button_4_out), .reset(C_out));  // open: out_3
  _16_bit_addition u_16_bit_addition_1 (
    .in_2(in_4[15]), .in_3(in_4[14]), .in_5(in_4[13]), .in_6(in_4[12]), .in_13(in_4[11]), .in_15(in_4[10]),
    .in_16(in_4[9]), .in_18(in_4[8]), .in_21(in_4[7]), .in_23(in_4[6]), .in_24(in_4[5]), .in_26(in_4[4]),
    .in_29(in_4[3]), .in_30(in_4[2]), .in_31(in_4[1]), .in_32(in_4[0]), .out_34(out_7), .out_35(out_6[15]),
    .out_36(out_6[14]), .out_37(out_6[13]), .out_38(out_6[12]), .out_39(out_6[11]), .out_40(out_6[10]),
    .out_41(out_6[9]), .out_42(out_6[8]), .out_43(out_6[7]), .out_44(out_6[6]), .out_45(out_6[5]),
    .out_46(out_6[4]), .out_47(out_6[3]), .out_48(out_6[2]), .out_49(out_6[1]), .out_50(out_6[0]),
    .in_33(1'b0), .in_1(in_5[15]), .in_4(in_5[14]), .in_7(in_5[13]), .in_8(in_5[12]), .in_9(in_5[11]),
    .in_10(in_5[10]), .in_11(in_5[9]), .in_12(in_5[8]), .in_14(in_5[7]), .in_17(in_5[6]), .in_19(in_5[5]),
    .in_20(in_5[4]), .in_22(in_5[3]), .in_25(in_5[2]), .in_27(in_5[1]), .in_28(in_5[0]));
  _4_bit_to_bool u_4_bit_to_bool_1 (.in_1(_4_bit_out_2), .out_2(n4_bit_to_bool_1_out_2));
  not not_1 (not_1_out, n4_bit_to_bool_1_out_2);
  _8_counter u_8_counter_1 (
    .in_1(not_1_out), .in_2(C_out), .out_3(n8_counter_1_out_3), .out_4(n8_counter_1_out_4),
    .out_5(n8_counter_1_out_5), .out_6(n8_counter_1_out_6), .out_7(n8_counter_1_out_7),
    .out_8(n8_counter_1_out_8), .out_9(n8_counter_1_out_9), .out_10(n8_counter_1_out_10));
  _4_bit_storage u_4_bit_storage_1 (.in_1(n4_bit_gateway_1_out_3), .in_2(C_out), .out_3(n4_bit_storage_1_out_3));
  _4_bit_gateway u_4_bit_gateway_1 (.in_1(_4_bit_out_2), .in_2(n8_counter_1_out_3), .out_3(n4_bit_gateway_1_out_3));
  _4_bit_gateway u_4_bit_gateway_2 (.in_1(_4_bit_out_2), .in_2(n8_counter_1_out_4), .out_3(n4_bit_gateway_2_out_3));
  _4_bit_storage u_4_bit_storage_2 (.in_1(n4_bit_gateway_2_out_3), .in_2(C_out), .out_3(n4_bit_storage_2_out_3));
  _4_bit_storage u_4_bit_storage_3 (.in_1(n4_bit_gateway_3_out_3), .in_2(C_out), .out_3(n4_bit_storage_3_out_3));
  _4_bit_gateway u_4_bit_gateway_3 (.in_1(_4_bit_out_2), .in_2(n8_counter_1_out_5), .out_3(n4_bit_gateway_3_out_3));
  _4_bit_storage u_4_bit_storage_4 (.in_1(n4_bit_gateway_4_out_3), .in_2(C_out), .out_3(n4_bit_storage_4_out_3));
  _4_bit_gateway u_4_bit_gateway_4 (.in_1(_4_bit_out_2), .in_2(n8_counter_1_out_6), .out_3(n4_bit_gateway_4_out_3));
  _4_bit_storage u_4_bit_storage_5 (.in_1(n4_bit_gateway_5_out_3), .in_2(C_out), .out_3(n4_bit_storage_5_out_3));
  _4_bit_gateway u_4_bit_gateway_5 (.in_1(_4_bit_out_2), .in_2(n8_counter_1_out_7), .out_3(n4_bit_gateway_5_out_3));
  _4_bit_gateway u_4_bit_gateway_6 (.in_1(_4_bit_out_2), .in_2(n8_counter_1_out_8), .out_3(n4_bit_gateway_6_out_3));
  _4_bit_storage u_4_bit_storage_6 (.in_1(n4_bit_gateway_6_out_3), .in_2(C_out), .out_3(n4_bit_storage_6_out_3));
  _4_bit_storage u_4_bit_storage_7 (.in_1(n4_bit_gateway_7_out_3), .in_2(C_out), .out_3(n4_bit_storage_7_out_3));
  _4_bit_gateway u_4_bit_gateway_7 (.in_1(_4_bit_out_2), .in_2(n8_counter_1_out_9), .out_3(n4_bit_gateway_7_out_3));
  _4_bit_storage u_4_bit_storage_8 (.in_1(n4_bit_gateway_8_out_3), .in_2(C_out), .out_3(n4_bit_storage_8_out_3));
  _4_bit_gateway u_4_bit_gateway_8 (.in_1(_4_bit_out_2), .in_2(n8_counter_1_out_10), .out_3(n4_bit_gateway_8_out_3));
  counter counter_1 (.store(in_1), .reset(in_2), .out_3(counter_1_out_3[0]), .out_4(counter_1_out_4));
  _4_bit_to_base10 u_4_bit_to_base10_1 (.in_1(n4_bit_storage_1_out_3), .out_2(n4_bit_to_base10_1_out_2));
  counter counter_2 (.store(counter_1_out_4), .reset(in_2), .out_3(counter_1_out_3[1]), .out_4(counter_2_out_4));
  base10_to_display base10_to_display_1 (.in_1(n4_bit_to_base10_1_out_2), .out_2(base10_to_display_1_out_2));
  _4_bit_to_base10 u_4_bit_to_base10_2 (.in_1(n4_bit_storage_2_out_3), .out_2(n4_bit_to_base10_2_out_2));
  base10_to_display base10_to_display_2 (.in_1(n4_bit_to_base10_2_out_2), .out_2(base10_to_display_2_out_2));
  base10_to_display base10_to_display_3 (.in_1(n4_bit_to_base10_3_out_2), .out_2(base10_to_display_3_out_2));
  _4_bit_to_base10 u_4_bit_to_base10_3 (.in_1(n4_bit_storage_3_out_3), .out_2(n4_bit_to_base10_3_out_2));
  _4_bit_to_base10 u_4_bit_to_base10_4 (.in_1(n4_bit_storage_4_out_3), .out_2(n4_bit_to_base10_4_out_2));
  base10_to_display base10_to_display_4 (.in_1(n4_bit_to_base10_4_out_2), .out_2(base10_to_display_4_out_2));
  base10_to_display base10_to_display_5 (
    .in_1(n4_bit_to_base10_5_out_2), .out_2({base10_to_display_5_out_2_2, base10_to_display_5_out_2}));
  _4_bit_to_base10 u_4_bit_to_base10_5 (.in_1(n4_bit_storage_5_out_3), .out_2(n4_bit_to_base10_5_out_2));
  _4_bit_to_base10 u_4_bit_to_base10_6 (.in_1(n4_bit_storage_6_out_3), .out_2(n4_bit_to_base10_6_out_2));
  base10_to_display base10_to_display_6 (
    .in_1(n4_bit_to_base10_6_out_2), .out_2({base10_to_display_6_out_2_2, base10_to_display_6_out_2}));
  _4_bit_to_base10 u_4_bit_to_base10_7 (.in_1(n4_bit_storage_7_out_3), .out_2(n4_bit_to_base10_7_out_2));
  _4_bit_to_base10 u_4_bit_to_base10_8 (.in_1(n4_bit_storage_8_out_3), .out_2(n4_bit_to_base10_8_out_2));
  counter counter_3 (.store(counter_2_out_4), .reset(in_2), .out_3(counter_1_out_3[2]));  // open: out_4
  base10_to_display base10_to_display_7 (
    .in_1(n4_bit_to_base10_7_out_2), .out_2({base10_to_display_7_out_2_2, base10_to_display_7_out_2}));
  base10_to_display base10_to_display_8 (.in_1(n4_bit_to_base10_8_out_2), .out_2(base10_to_display_8_out_2));
  _4_bit_to_base10 u_4_bit_to_base10_9 (.in_1({in_3, counter_1_out_3}), .out_2(n4_bit_to_base10_9_out_2));
  _7_Segment_Display u_7_segment_display_1 (
    .g(base10_to_display_2_out_2[3]), .f(base10_to_display_2_out_2[2]), .a(base10_to_display_2_out_2[1]),
    .b(base10_to_display_2_out_2[0]), .e(base10_to_display_2_out_2[4]), .d(base10_to_display_2_out_2[5]),
    .c(base10_to_display_2_out_2[6]));  // open: dp
  _7_Segment_Display u_7_segment_display_2 (
    .g(base10_to_display_1_out_2[3]), .f(base10_to_display_1_out_2[2]), .a(base10_to_display_1_out_2[1]),
    .b(base10_to_display_1_out_2[0]), .e(base10_to_display_1_out_2[4]), .d(base10_to_display_1_out_2[5]),
    .c(base10_to_display_1_out_2[6]));  // open: dp
  base10_to_display base10_to_display_9 (.in_1(n4_bit_to_base10_9_out_2), .out_2(base10_to_display_9_out_2));
  _7_Segment_Display u_7_segment_display_3 (
    .g(base10_to_display_3_out_2[3]), .f(base10_to_display_3_out_2[2]), .a(base10_to_display_3_out_2[1]),
    .b(base10_to_display_3_out_2[0]), .e(base10_to_display_3_out_2[4]), .d(base10_to_display_3_out_2[5]),
    .c(base10_to_display_3_out_2[6]));  // open: dp
  _7_Segment_Display u_7_segment_display_4 (
    .g(base10_to_display_4_out_2[3]), .f(base10_to_display_4_out_2[2]), .a(base10_to_display_4_out_2[1]),
    .b(base10_to_display_4_out_2[0]), .e(base10_to_display_4_out_2[4]), .d(base10_to_display_4_out_2[5]),
    .c(base10_to_display_4_out_2[6]));  // open: dp
  _7_Segment_Display u_7_segment_display_5 (
    .g(base10_to_display_9_out_2[3]), .f(base10_to_display_9_out_2[2]), .a(base10_to_display_9_out_2[1]),
    .b(base10_to_display_9_out_2[0]), .e(base10_to_display_9_out_2[4]), .d(base10_to_display_9_out_2[5]),
    .c(base10_to_display_9_out_2[6]));  // open: dp
  _7_Segment_Display u_7_segment_display_6 (
    .g(base10_to_display_6_out_2[3]), .f(base10_to_display_6_out_2[2]), .a(base10_to_display_6_out_2[1]),
    .b(base10_to_display_6_out_2[0]), .e(base10_to_display_6_out_2_2[0]), .d(base10_to_display_6_out_2_2[1]),
    .c(base10_to_display_6_out_2_2[2]));  // open: dp
  _7_Segment_Display u_7_segment_display_7 (
    .g(base10_to_display_5_out_2[3]), .f(base10_to_display_5_out_2[2]), .a(base10_to_display_5_out_2[1]),
    .b(base10_to_display_5_out_2[0]), .e(base10_to_display_5_out_2_2[0]), .d(base10_to_display_5_out_2_2[1]),
    .c(base10_to_display_5_out_2_2[2]));  // open: dp
  _7_Segment_Display u_7_segment_display_8 (
    .g(base10_to_display_7_out_2[3]), .f(base10_to_display_7_out_2[2]), .a(base10_to_display_7_out_2[1]),
    .b(base10_to_display_7_out_2[0]), .e(base10_to_display_7_out_2_2[0]), .d(base10_to_display_7_out_2_2[1]),
    .c(base10_to_display_7_out_2_2[2]));  // open: dp
  _7_Segment_Display u_7_segment_display_9 (
    .g(base10_to_display_8_out_2[3]), .f(base10_to_display_8_out_2[2]), .a(base10_to_display_8_out_2[1]),
    .b(base10_to_display_8_out_2[0]), .e(base10_to_display_8_out_2[4]), .d(base10_to_display_8_out_2[5]),
    .c(base10_to_display_8_out_2[6]));  // open: dp
endmodule

module _1_bit_sum (
  input  in_1,
  input  in_2,
  input  in_3,
  output out_4,
  output out_5
);

  wire and_1_out, and_2_out, and_3_out, and_4_out, and_5_out, not_1_out, or_1_out;

  and and_1 (and_1_out, in_1, in_2);
  and and_2 (and_2_out, in_1, in_3);
  and and_3 (and_3_out, in_2, in_3);
  not not_1 (not_1_out, out_4);
  or or_1 (or_1_out, in_1, in_2, in_3);
  or or_2 (out_4, and_1_out, and_2_out, and_3_out);
  and and_4 (and_4_out, and_2_out, and_3_out);
  and and_5 (and_5_out, not_1_out, or_1_out);
  or or_3 (out_5, and_4_out, and_5_out);
endmodule

module _4_bit_sum (
  input  in_1,
  input  in_2,
  input  in_3,
  input  in_4,
  input  in_5,
  input  in_6,
  input  in_7,
  input  in_8,
  input  in_9,
  output out_10,
  output out_11,
  output out_12,
  output out_13,
  output out_14
);

  wire n1_bit_sum_2_out_4, n1_bit_sum_3_out_4, n1_bit_sum_4_out_4;

  _1_bit_sum u_1_bit_sum_1 (.in_1(in_1), .in_2(in_5), .out_4(out_10), .in_3(n1_bit_sum_2_out_4), .out_5(out_11));
  _1_bit_sum u_1_bit_sum_2 (
    .in_1(in_2), .in_2(in_6), .out_4(n1_bit_sum_2_out_4), .in_3(n1_bit_sum_3_out_4), .out_5(out_12));
  _1_bit_sum u_1_bit_sum_3 (
    .in_1(in_3), .in_2(in_7), .out_4(n1_bit_sum_3_out_4), .in_3(n1_bit_sum_4_out_4), .out_5(out_13));
  _1_bit_sum u_1_bit_sum_4 (.in_1(in_4), .in_2(in_8), .out_4(n1_bit_sum_4_out_4), .in_3(in_9), .out_5(out_14));
endmodule

module _16_bit_addition (
  input  in_1,
  input  in_2,
  input  in_3,
  input  in_4,
  input  in_5,
  input  in_6,
  input  in_7,
  input  in_8,
  input  in_9,
  input  in_10,
  input  in_11,
  input  in_12,
  input  in_13,
  input  in_14,
  input  in_15,
  input  in_16,
  input  in_17,
  input  in_18,
  input  in_19,
  input  in_20,
  input  in_21,
  input  in_22,
  input  in_23,
  input  in_24,
  input  in_25,
  input  in_26,
  input  in_27,
  input  in_28,
  input  in_29,
  input  in_30,
  input  in_31,
  input  in_32,
  input  in_33,
  output out_34,
  output out_35,
  output out_36,
  output out_37,
  output out_38,
  output out_39,
  output out_40,
  output out_41,
  output out_42,
  output out_43,
  output out_44,
  output out_45,
  output out_46,
  output out_47,
  output out_48,
  output out_49,
  output out_50
);

  wire n4_bit_sum_2_out_10, n4_bit_sum_3_out_10, n4_bit_sum_4_out_10;

  _4_bit_sum u_4_bit_sum_1 (
    .in_1(in_1), .in_2(in_4), .in_3(in_7), .in_4(in_8), .in_5(in_2), .in_6(in_3), .in_7(in_5), .in_8(in_6),
    .out_10(out_34), .in_9(n4_bit_sum_2_out_10), .out_11(out_35), .out_12(out_36), .out_13(out_37),
    .out_14(out_38));
  _4_bit_sum u_4_bit_sum_2 (
    .in_1(in_9), .in_2(in_10), .in_3(in_11), .in_4(in_12), .in_5(in_13), .in_6(in_15), .in_7(in_16),
    .in_8(in_18), .out_10(n4_bit_sum_2_out_10), .in_9(n4_bit_sum_3_out_10), .out_11(out_39), .out_12(out_40),
    .out_13(out_41), .out_14(out_42));
  _4_bit_sum u_4_bit_sum_3 (
    .in_1(in_14), .in_2(in_17), .in_3(in_19), .in_4(in_20), .in_5(in_21), .in_6(in_23), .in_7(in_24),
    .in_8(in_26), .out_10(n4_bit_sum_3_out_10), .in_9(n4_bit_sum_4_out_10), .out_11(out_43), .out_12(out_44),
    .out_13(out_45), .out_14(out_46));
  _4_bit_sum u_4_bit_sum_4 (
    .in_1(in_22), .in_2(in_25), .in_3(in_27), .in_4(in_28), .in_5(in_29), .in_6(in_30), .in_7(in_31),
    .in_8(in_32), .out_10(n4_bit_sum_4_out_10), .in_9(in_33), .out_11(out_47), .out_12(out_48),
    .out_13(out_49), .out_14(out_50));
endmodule

module _4_bit_to_base10 (
  input  [3:0] in_1,
  output [9:0] out_2
);

  wire not_1_out, not_2_out, not_3_out, not_4_out, not_5_out, not_6_out, not_7_out, not_8_out, not_9_out,
       not_10_out, not_11_out, not_12_out, not_13_out, not_14_out, not_15_out, not_16_out, not_17_out,
       not_18_out, not_19_out, not_20_out, not_21_out, not_22_out, not_23_out, not_24_out, not_25_out;

  not not_1 (not_1_out, in_1[0]);
  not not_2 (not_2_out, in_1[1]);
  not not_3 (not_3_out, in_1[2]);
  not not_4 (not_4_out, in_1[3]);
  not not_5 (not_5_out, in_1[1]);
  not not_6 (not_6_out, in_1[2]);
  not not_7 (not_7_out, in_1[3]);
  not not_8 (not_8_out, in_1[0]);
  not not_9 (not_9_out, in_1[2]);
  not not_10 (not_10_out, in_1[3]);
  not not_11 (not_11_out, in_1[2]);
  not not_12 (not_12_out, in_1[3]);
  not not_13 (not_13_out, in_1[0]);
  not not_14 (not_14_out, in_1[1]);
  not not_15 (not_15_out, in_1[3]);
  not not_16 (not_16_out, in_1[1]);
  not not_17 (not_17_out, in_1[3]);
  not not_18 (not_18_out, in_1[0]);
  not not_19 (not_19_out, in_1[3]);
  not not_20 (not_20_out, in_1[3]);
  not not_21 (not_21_out, in_1[0]);
  not not_22 (not_22_out, in_1[1]);
  not not_23 (not_23_out, in_1[2]);
  not not_24 (not_24_out, in_1[1]);
  not not_25 (not_25_out, in_1[2]);
  and and_1 (out_2[0], not_1_out, not_2_out, not_3_out, not_4_out);
  and and_2 (out_2[1], in_1[0], not_5_out, not_6_out, not_7_out);
  and and_3 (out_2[2], not_8_out, in_1[1], not_9_out, not_10_out);
  and and_4 (out_2[3], in_1[0], in_1[1], not_11_out, not_12_out);
  and and_5 (out_2[4], not_13_out, not_14_out, in_1[2], not_15_out);
  and and_6 (out_2[5], in_1[0], not_16_out, in_1[2], not_17_out);
  and and_7 (out_2[6], not_18_out, in_1[1], in_1[2], not_19_out);
  and and_8 (out_2[7], in_1[0], in_1[1], in_1[2], not_20_out);
  and and_9 (out_2[8], not_21_out, not_22_out, not_23_out, in_1[3]);
  and and_10 (out_2[9], in_1[0], not_24_out, not_25_out, in_1[3]);
endmodule

module base10_to_display (
  input  [9:0] in_1,
  output [6:0] out_2
);

  or or_1 (out_2[0], in_1[0], in_1[1], in_1[2], in_1[3], in_1[4], in_1[7], in_1[8], in_1[9]);
  or or_2 (out_2[2], in_1[0], in_1[4], in_1[5], in_1[6], in_1[8], in_1[9]);
  or or_3 (out_2[1], in_1[0], in_1[2], in_1[3], in_1[5], in_1[6], in_1[7], in_1[8], in_1[9]);
  or or_4 (out_2[3], in_1[3], in_1[4], in_1[5], in_1[2], in_1[6], in_1[8], in_1[9]);
  or or_5 (out_2[4], in_1[0], in_1[2], in_1[6], in_1[8]);
  or or_6 (out_2[5], in_1[0], in_1[2], in_1[3], in_1[5], in_1[6], in_1[8], in_1[9]);
  or or_7 (out_2[6], in_1[0], in_1[1], in_1[3], in_1[4], in_1[5], in_1[6], in_1[7], in_1[8], in_1[9]);
  _7_Segment_Display u_7_segment_display_1 (
    .g(out_2[3]), .f(out_2[2]), .a(out_2[1]), .b(out_2[0]), .e(out_2[4]), .d(out_2[5]), .c(out_2[6]));  // open: dp
endmodule

module bit_storage (
  input  store,
  input  reset,
  output out_3
);

  wire not_1_out, not_2_out, or_2_out;

  not not_1 (not_1_out, or_2_out);
  not not_2 (not_2_out, out_3);
  or or_1 (out_3, not_1_out, store);
  or or_2 (or_2_out, not_2_out, reset);
endmodule

module base10_to_4_bit (
  input  [9:0] in_1,
  output [3:0] out_2
);

  or or_1 (out_2[0], in_1[1], in_1[3], in_1[5], in_1[7], in_1[9]);
  or or_2 (out_2[1], in_1[2], in_1[6], in_1[7], in_1[3]);
  or or_3 (out_2[2], in_1[4], in_1[5], in_1[6], in_1[7]);
  or or_4 (out_2[3], in_1[8], in_1[9]);
endmodule

module _4_bit_storage (
  input  [3:0] in_1,
  input  in_2,
  output [3:0] out_3
);

  bit_storage bit_storage_1 (.store(in_1[0]), .reset(in_2), .out_3(out_3[0]));
  bit_storage bit_storage_2 (.store(in_1[1]), .reset(in_2), .out_3(out_3[1]));
  bit_storage bit_storage_3 (.store(in_1[2]), .reset(in_2), .out_3(out_3[2]));
  bit_storage bit_storage_4 (.store(in_1[3]), .reset(in_2), .out_3(out_3[3]));
endmodule

module counter (
  input  store,
  input  reset,
  output out_3,
  output out_4
);

  wire and_1_out, and_2_out, and_3_out, and_4_out, and_5_out, bit_storage_2_out_3, bit_storage_4_out_3,
       not_1_out, not_2_out, not_3_out, or_1_out, or_2_out, or_3_out;

  or or_1 (or_1_out, and_5_out, reset);
  not not_1 (not_1_out, out_3);
  and and_1 (and_1_out, not_1_out, store);
  or or_2 (or_2_out, or_1_out, out_3);
  bit_storage bit_storage_1 (.store(and_1_out), .reset(or_2_out), .out_3(out_4));
  not not_2 (not_2_out, store);
  or or_3 (or_3_out, out_4, or_1_out);
  bit_storage bit_storage_2 (.store(and_3_out), .reset(or_1_out), .out_3(bit_storage_2_out_3));
  and and_2 (and_2_out, store, bit_storage_2_out_3);
  and and_3 (and_3_out, not_2_out, out_4);
  bit_storage bit_storage_3 (.store(and_2_out), .reset(or_3_out), .out_3(out_3));
  and and_4 (and_4_out, not_3_out, out_3);
  not not_3 (not_3_out, store);
  bit_storage bit_storage_4 (.store(and_4_out), .reset(or_1_out), .out_3(bit_storage_4_out_3));
  and and_5 (and_5_out, store, bit_storage_4_out_3);
endmodule

module _8_counter (
  input  in_1,
  input  in_2,
  output out_3,
  output out_4,
  output out_5,
  output out_6,
  output out_7,
  output out_8,
  output out_9,
  output out_10
);

  wire counter_1_out_4, counter_2_out_4;
  wire [2:0] counter_1_out_3;
  wire [9:8] n4_bit_to_base10_1_out_2;

  counter counter_1 (.store(in_1), .reset(in_2), .out_3(counter_1_out_3[0]), .out_4(counter_1_out_4));
  counter counter_2 (.store(counter_1_out_4), .reset(in_2), .out_3(counter_1_out_3[1]), .out_4(counter_2_out_4));
  counter counter_3 (.store(counter_2_out_4), .reset(in_2), .out_3(counter_1_out_3[2]));  // open: out_4
  _4_bit_to_base10 u_4_bit_to_base10_1 (
    .in_1({1'b0, counter_1_out_3}),
    .out_2({n4_bit_to_base10_1_out_2, out_10, out_9, out_8, out_7, out_6, out_5, out_4, out_3}));
endmodule

module _4_bit_to_bool (
  input  [3:0] in_1,
  output out_2
);

  or or_1 (out_2, in_1[0], in_1[1], in_1[2], in_1[3]);
endmodule

module _4_bit_gateway (
  input  [3:0] in_1,
  input  in_2,
  output [3:0] out_3
);

  and and_1 (out_3[0], in_1[0], in_2);
  and and_2 (out_3[1], in_1[1], in_2);
  and and_3 (out_3[2], in_1[2], in_2);
  and and_4 (out_3[3], in_1[3], in_2);
endmodule

module input_number (
  input  [3:0] in_1,
  input  in_2,
  output [3:0] out_3,
  output [3:0] out_4,
  output [3:0] out_5
);

  wire n4_bit_to_bool_1_out_2, n4_bit_to_bool_2_out_2, n4_bit_to_bool_3_out_2, n4_bit_to_bool_4_out_2,
       not_1_out, not_2_out, not_3_out, not_4_out, or_1_out, or_2_out, or_3_out;
  wire [3:0] n4_bit_gateway_1_out_3, n4_bit_gateway_2_out_3, n4_bit_gateway_3_out_3, n4_bit_gateway_4_out_3,
       n4_bit_gateway_5_out_3, n4_bit_gateway_6_out_3, n4_bit_storage_1_out_3, n4_bit_storage_2_out_3,
       n4_bit_storage_3_out_3;

  _4_bit_to_bool u_4_bit_to_bool_1 (.in_1(in_1), .out_2(n4_bit_to_bool_1_out_2));
  not not_1 (not_1_out, n4_bit_to_bool_1_out_2);
  not not_2 (not_2_out, n4_bit_to_bool_1_out_2);
  not not_3 (not_3_out, n4_bit_to_bool_1_out_2);
  not not_4 (not_4_out, n4_bit_to_bool_1_out_2);
  _4_bit_to_bool u_4_bit_to_bool_2 (.in_1(out_3), .out_2(n4_bit_to_bool_2_out_2));
  or or_1 (or_1_out, n4_bit_to_bool_2_out_2, in_2);
  _4_bit_gateway u_4_bit_gateway_1 (.in_1(out_4), .in_2(not_1_out), .out_3(n4_bit_gateway_1_out_3));
  _4_bit_to_bool u_4_bit_to_bool_3 (.in_1(out_4), .out_2(n4_bit_to_bool_3_out_2));
  or or_2 (or_2_out, n4_bit_to_bool_3_out_2, in_2);
  _4_bit_gateway u_4_bit_gateway_2 (.in_1(out_5), .in_2(not_2_out), .out_3(n4_bit_gateway_2_out_3));
  _4_bit_to_bool u_4_bit_to_bool_4 (.in_1(out_5), .out_2(n4_bit_to_bool_4_out_2));
  or or_3 (or_3_out, n4_bit_to_bool_4_out_2, in_2);
  _4_bit_gateway u_4_bit_gateway_3 (.in_1(in_1), .in_2(not_3_out), .out_3(n4_bit_gateway_3_out_3));
  _4_bit_storage u_4_bit_storage_1 (.in_1(n4_bit_gateway_1_out_3), .in_2(or_1_out), .out_3(n4_bit_storage_1_out_3));
  _4_bit_storage u_4_bit_storage_2 (.in_1(n4_bit_gateway_2_out_3), .in_2(or_2_out), .out_3(n4_bit_storage_2_out_3));
  _4_bit_storage u_4_bit_storage_3 (.in_1(n4_bit_gateway_3_out_3), .in_2(or_3_out), .out_3(n4_bit_storage_3_out_3));
  _4_bit_storage u_4_bit_storage_4 (.in_1(n4_bit_gateway_4_out_3), .in_2(not_4_out), .out_3(out_3));
  _4_bit_gateway u_4_bit_gateway_4 (
    .in_1(n4_bit_storage_1_out_3), .in_2(n4_bit_to_bool_1_out_2), .out_3(n4_bit_gateway_4_out_3));
  _4_bit_storage u_4_bit_storage_5 (.in_1(n4_bit_gateway_5_out_3), .in_2(not_4_out), .out_3(out_4));
  _4_bit_gateway u_4_bit_gateway_5 (
    .in_1(n4_bit_storage_2_out_3), .in_2(n4_bit_to_bool_1_out_2), .out_3(n4_bit_gateway_5_out_3));
  _4_bit_storage u_4_bit_storage_6 (.in_1(n4_bit_gateway_6_out_3), .in_2(not_4_out), .out_3(out_5));
  _4_bit_gateway u_4_bit_gateway_6 (
    .in_1(n4_bit_storage_3_out_3), .in_2(n4_bit_to_bool_1_out_2), .out_3(n4_bit_gateway_6_out_3));
endmodule
